# Fritzing sketch Reflektor (saved by Fritzing 0.8.3b)
breadboards: 2

parts:
  Brain = Arduino Uno (Rev3)
  Audio = Arduino Uno (Rev3)  # not connected
  U1 = 74HC595 [package="DIP16 [THT]"]
  U2 = 74HC595 [package="DIP16 [THT]"]
  IC1 = L293D [package=THT]
  IC2 = L293D [package=THT]
  IC3 = L293D [package=THT]
  IC4 = L293D [package=THT]
  J7 = screw terminal, 4 pins
  J1 = screw terminal, 4 pins
  J3 = screw terminal, 4 pins
  J5 = screw terminal, 4 pins
  J8 = female pin header, 5 pins [form="♀ (female)"]
  U3 = 74HC595 [package="DIP16 [THT]"]
  J9 = screw terminal, 16 pins
  J10 = Screw terminal - 2 pins [package=THT]
  J11 = Screw terminal - 2 pins [package=THT]

nets:
  N1: Brain.D8, U2.DS, J8.pin1
  N2: Brain.D9_PWM, U1.ST_CP, U2.ST_CP, J8.pin2, U3.ST_CP
  N3: Brain.D7, U1.SH_CP, U2.SH_CP, J8.pin3, U3.SH_CP
  N4: U1.Q1, IC2.In_2
  N5: U1.Q2, IC2.In_1
  N6: U1.Q3, IC2.In_4
  N7: U1.Q4, IC1.In_3
  N8: U1.Q5, IC1.In_2
  N9: U1.Q6, IC1.In_1
  N10: U1.Q7, IC1.In_4
  GND: U1.GND, U1.OE, U2.GND, U2.OE, IC1.0V, IC2.0V, IC3.0V, IC4.0V, J8.pin4, U3.GND, U3.OE, J9.pin1, J9.pin3, J9.pin5, J9.pin7, J9.pin9, J9.pin11, J9.pin13, J9.pin15, J10.pin2, J11.pin2
  N11: U1.Q7', U3.DS
  VCC: U1.MR, U1.VCC, U2.MR, U2.VCC, IC1.Enable_1, IC1.Enable_2, IC1.+V, IC2.Enable_1, IC2.+Vmotor, IC2.Enable_2, IC2.+V, IC3.Enable_1, IC3.+Vmotor, IC3.Enable_2, IC3.+V, IC4.Enable_1, IC4.+Vmotor, IC4.Enable_2, IC4.+V, J8.pin5, U3.MR, U3.VCC, J10.pin1
  N12: U1.DS, U2.Q7'
  N13: U1.Q0, IC2.In_3
  N14: U2.Q1, IC4.In_2
  N15: U2.Q2, IC4.In_1
  N16: U2.Q3, IC4.In_4
  N17: U2.Q4, IC3.In_3
  N18: U2.Q5, IC3.In_2
  N19: U2.Q6, IC3.In_1
  N20: U2.Q7, IC3.In_4
  N21: U2.Q0, IC4.In_3
  N22: IC1.Out_1_(_Controlled_by_Enable_1_), J7.pin2
  N23: IC1.Out_2_(_Controlled_by_Enable_1_), J7.pin3
  N24: IC1.+Vmotor, J11.pin1
  N25: IC1.Out_3_(_Controlled_by_Enable_2_), J7.pin4
  N26: IC1.Out_4_(_Controlled_by_Enable_2_), J7.pin1
  N27: IC2.Out_1_(_Controlled_by_Enable_1_), J1.pin2
  N28: IC2.Out_2_(_Controlled_by_Enable_1_), J1.pin3
  N29: IC2.Out_3_(_Controlled_by_Enable_2_), J1.pin4
  N30: IC2.Out_4_(_Controlled_by_Enable_2_), J1.pin1
  N31: IC3.Out_1_(_Controlled_by_Enable_1_), J3.pin2
  N32: IC3.Out_2_(_Controlled_by_Enable_1_), J3.pin3
  N33: IC3.Out_3_(_Controlled_by_Enable_2_), J3.pin4
  N34: IC3.Out_4_(_Controlled_by_Enable_2_), J3.pin1
  N35: IC4.Out_1_(_Controlled_by_Enable_1_), J5.pin2
  N36: IC4.Out_2_(_Controlled_by_Enable_1_), J5.pin3
  N37: IC4.Out_3_(_Controlled_by_Enable_2_), J5.pin4
  N38: IC4.Out_4_(_Controlled_by_Enable_2_), J5.pin1
  N39: U3.Q1, J9.pin14
  N40: U3.Q2, J9.pin12
  N41: U3.Q3, J9.pin10
  N42: U3.Q4, J9.pin8
  N43: U3.Q5, J9.pin6
  N44: U3.Q6, J9.pin4
  N45: U3.Q7, J9.pin2
  N46: U3.Q0, J9.pin16

notes:
  Stepper 1: 12v
  Steppers 2,3,4: 5v
  12v
  5v
